# Fritzing sketch Dht22 (saved by Fritzing 0.9.3b)
circuit board: 8.21608cm x 10.0854cm
breadboards: 1

parts:
  Raspberry_Pi_1 = Raspberry Pi 3 [part_number=RPI-3-V1.2]
  DHT22 = Humidity and Temperature Sensor Dht22 or AM2303
  R1_10kΩ = Resistor [tolerance=±5% resistance=220 package=THT]

nets:
  3V3: Raspberry_Pi_1.3v3, Raspberry_Pi_1.GPIO2, Raspberry_Pi_1.5V, DHT22.Vcc, R1_10kΩ.Pin_1
  N1: Raspberry_Pi_1.GPIO3, Raspberry_Pi_1.GIPO4, Raspberry_Pi_1.GND, Raspberry_Pi_1.GIPO18, Raspberry_Pi_1.GIPO15, Raspberry_Pi_1.GIPO14, DHT22.Data-signal, DHT22.GND_1, R1_10kΩ.Pin_0
  N2: Raspberry_Pi_1.GIPO17, Raspberry_Pi_1.GIPO27
  N3: Raspberry_Pi_1.GIPO22, Raspberry_Pi_1.GIPO24
  N4: Raspberry_Pi_1.GIPO10, Raspberry_Pi_1.GIPO25
  N5: Raspberry_Pi_1.GIPO11, Raspberry_Pi_1.GIPO7

custom parts:
  Humidity and Temperature Sensor Dht22 or AM2303: Digital relative humidity & temperature sensor Dht22
