# Fritzing sketch BoardDht11Dht22Lcd1602Button (saved by Fritzing 0.9.3b)
circuit board: 8.21608cm x 10.0854cm
breadboards: 1

parts:
  Raspberry_Pi_1 = Raspberry Pi 3 [part_number=RPI-3-V1.2]
  DHT22 = Humidity and Temperature Sensor Dht22 or AM2303
  DHT11 = Humidity and Temperature Sensor RHT03
  R2_10kΩ = Resistor [tolerance=±5% resistance=220 package=THT]
  LCD_1602 = LCD screen
  R3 = Trimmer Potentiometer [maximum_resistance=10kΩ package=THT]
  R1_10kΩ = Resistor [tolerance=±5% resistance=220 package=THT]
  S1 = Pushbutton [package="[THT]"]

nets:
  GND: Raspberry_Pi_1.GPIO3, Raspberry_Pi_1.GIPO4, Raspberry_Pi_1.GND, Raspberry_Pi_1.GIPO18, Raspberry_Pi_1.GIPO15, Raspberry_Pi_1.GIPO14, DHT22.Data-signal, DHT22.GND_1, DHT11.GND_2, LCD_1602.VSS, LCD_1602.R/W, LCD_1602.DB7, LCD_1602.LED-, R3.leg2, R1_10kΩ.Pin_0
  N1: Raspberry_Pi_1.GIPO17, Raspberry_Pi_1.GIPO27, DHT11.Data-signal, R2_10kΩ.Pin_0
  N2: Raspberry_Pi_1.GIPO22, Raspberry_Pi_1.GIPO24, LCD_1602.DB5, S1.Pin_1, S1.Pin_2
  N3: Raspberry_Pi_1.GIPO10, Raspberry_Pi_1.GIPO25, LCD_1602.DB4
  N4: Raspberry_Pi_1.GIPO9, Raspberry_Pi_1.GIPO8, LCD_1602.E
  N5: Raspberry_Pi_1.GIPO11, Raspberry_Pi_1.GIPO7, LCD_1602.RS
  N6: Raspberry_Pi_1.GIPO23, LCD_1602.DB6
  VCC: Raspberry_Pi_1.5V, DHT22.Vcc, DHT11.Vcc, R2_10kΩ.Pin_1, LCD_1602.VDD, LCD_1602.LED+, R3.leg1, R1_10kΩ.Pin_1, S1.Pin_3, S1.Pin_4
  N7: LCD_1602.V0, R3.wiper

custom parts:
  Humidity and Temperature Sensor Dht22 or AM2303: Digital relative humidity & temperature sensor Dht22
